// Logisim project Parcial_1_Microcontroladores_Jose_Rueda.circ as structural Verilog: 5 circuits, main circuit top
module top (
  input  Reinicio,
  input  P,
  output [1:0] Luz_A,
  output [1:0] Luz_B,
  output Walk,
  output DontWalk
);

  wire decoder_1_out0, decoder_1_out1, decoder_1_out2, decoder_2_out0, decoder_2_out1, decoder_2_out2, N_out,
       Reloj_out, Trafico_A_out, Trafico_B_out;
  wire [2:0] moore_semaforo_block_1_s;

  Clock #(.highDuration(3), .lowDuration(3)) Trafico_A (.out(Trafico_A_out));
  Clock Reloj (.out(Reloj_out));
  Clock #(.highDuration(5), .lowDuration(5)) Trafico_B (.out(Trafico_B_out));
  Clock #(.highDuration(20), .lowDuration(20)) N (.out(N_out));
  moore_semaforo_block moore_semaforo_block_1 (
    .Trafico_A(Trafico_A_out), .Reloj(Reloj_out), .Reinicio(Reinicio), .Trafico_B(Trafico_B_out), .N(N_out),
    .Luz_A(Luz_A), .S(moore_semaforo_block_1_s), .Luz_B(Luz_B));
  mealy_peatonal_block mealy_peatonal_block_1 (
    .B2(moore_semaforo_block_1_s[2]), .B1(moore_semaforo_block_1_s[1]), .B0(moore_semaforo_block_1_s[0]),
    .P(P), .Walk(Walk), .DontWalk(DontWalk));
  Decoder #(.enable("false"), .select(2)) decoder_1 (
    .out0(decoder_1_out0), .out1(decoder_1_out1), .out2(decoder_1_out2), .sel(Luz_A));  // open: out3
  Decoder #(.enable("false"), .select(2)) decoder_2 (
    .out0(decoder_2_out0), .out1(decoder_2_out1), .out2(decoder_2_out2), .sel(Luz_B));  // open: out3
  LED led_1 (.in(decoder_1_out0));
  LED led_2 (.in(decoder_1_out1));
  LED led_3 (.in(decoder_1_out2));
  LED led_4 (.in(decoder_2_out0));
  LED led_5 (.in(decoder_2_out1));
  LED led_6 (.in(decoder_2_out2));
endmodule

module moore_semaforo_block (
  input  Trafico_A,
  input  Reloj,
  input  Reinicio,
  input  Trafico_B,
  input  N,
  output [1:0] Luz_A,
  output [2:0] S,
  output [1:0] Luz_B
);

  wire moore_next_state_logic_1_s0n, moore_next_state_logic_1_s1n, moore_next_state_logic_1_s2n;

  moore_next_state_logic moore_next_state_logic_1 (
    .B2(S[2]), .B1(S[1]), .B0(S[0]), .Trafico_A(Trafico_A), .Trafico_B(Trafico_B), .N(N),
    .S2n(moore_next_state_logic_1_s2n), .S1n(moore_next_state_logic_1_s1n), .S0n(moore_next_state_logic_1_s0n));
  D_Flip_Flop d_ff_1 (.D(moore_next_state_logic_1_s2n), .clk(Reloj), .Q(S[2]), .reset(Reinicio));  // open: Qn, preset
  D_Flip_Flop d_ff_2 (.D(moore_next_state_logic_1_s1n), .clk(Reloj), .Q(S[1]), .reset(Reinicio));  // open: Qn, preset
  D_Flip_Flop d_ff_3 (.D(moore_next_state_logic_1_s0n), .clk(Reloj), .Q(S[0]), .reset(Reinicio));  // open: Qn, preset
  moore_output_logic moore_output_logic_1 (
    .B2(S[2]), .B1(S[1]), .B0(S[0]), .LA1(Luz_A[1]), .LA0(Luz_A[0]), .LB1(Luz_B[1]), .LB0(Luz_B[0]));
endmodule

module moore_next_state_logic (
  input  B2,
  input  B1,
  input  B0,
  input  Trafico_A,
  input  Trafico_B,
  input  N,
  output S2n,
  output S1n,
  output S0n
);

  wire and_1_out, and_2_out, and_3_out, and_4_out, and_5_out, and_6_out, and_7_out, and_8_out, and_9_out,
       and_10_out, and_11_out, and_12_out, and_13_out, and_14_out, and_15_out, not_1_out, not_2_out,
       not_3_out, not_4_out, not_5_out;

  not not_1 (not_1_out, B2);
  not not_2 (not_2_out, B1);
  not not_3 (not_3_out, B0);
  not not_4 (not_4_out, Trafico_A);
  not not_5 (not_5_out, N);
  and and_1 (and_1_out, B2, not_2_out, not_3_out);
  and and_2 (and_2_out, not_2_out, not_3_out, N);
  and and_3 (and_3_out, B1, B0, N);
  and and_4 (and_4_out, B1, B0, Trafico_A);
  and and_5 (and_5_out, B2, not_3_out, N);
  and and_6 (and_6_out, not_1_out, N);
  and and_7 (and_7_out, not_1_out, not_2_out, B0);
  and and_8 (and_8_out, B1, N);
  and and_9 (and_9_out, not_1_out, not_3_out, Trafico_A, Trafico_B);
  and and_10 (and_10_out, not_1_out, B1, not_3_out);
  and and_11 (and_11_out, not_1_out, B1, not_4_out);
  and and_12 (and_12_out, B2, not_2_out, not_3_out);
  and and_13 (and_13_out, not_1_out, B1, not_3_out);
  and and_14 (and_14_out, not_1_out, not_3_out, Trafico_B, not_5_out);
  and and_15 (and_15_out, not_1_out, B1, not_4_out, not_5_out);
  or or_1 (S2n, and_1_out, and_2_out, and_3_out, and_4_out, and_5_out);
  or or_2 (S1n, and_6_out, and_7_out, and_8_out, and_9_out, and_10_out, and_11_out);
  or or_3 (S0n, and_12_out, and_13_out, and_14_out, and_15_out);
endmodule

module moore_output_logic (
  input  B2,
  input  B1,
  input  B0,
  output LA1,
  output LA0,
  output LB1,
  output LB0
);

  wire and_2_out, and_3_out, not_1_out, not_2_out, not_3_out;

  not not_1 (not_1_out, B2);
  not not_2 (not_2_out, B1);
  not not_3 (not_3_out, B0);
  and and_1 (LA1, not_1_out, not_2_out, not_3_out);
  and and_2 (and_2_out, not_1_out, not_2_out, B0);
  and and_3 (and_3_out, B2, B1);
  and and_4 (LB1, B1, B0);
  and and_5 (LB0, B2, not_3_out);
  or or_1 (LA0, and_2_out, and_3_out);
endmodule

module mealy_peatonal_block (
  input  B2,
  input  B1,
  input  B0,
  input  P,
  output Walk,
  output DontWalk
);

  wire and_1_out, and_2_out, and_3_out, and_4_out, and_5_out, not_1_out, not_2_out, not_3_out, not_4_out;

  not not_1 (not_1_out, B2);
  not not_2 (not_2_out, B1);
  not not_3 (not_3_out, B0);
  not not_4 (not_4_out, P);
  and and_1 (and_1_out, not_1_out, B1, not_3_out, P);
  and and_2 (and_2_out, B2, B0, P);
  and and_3 (and_3_out, not_1_out, B0);
  and and_4 (and_4_out, B2, not_3_out);
  and and_5 (and_5_out, not_1_out, not_2_out);
  or or_1 (Walk, and_1_out, and_2_out);
  or or_2 (DontWalk, not_4_out, and_3_out, and_4_out, and_5_out);
endmodule
